# Fritzing sketch LED Lamp Cap (saved by Fritzing 0.9.2b)
breadboards: 1

parts:
  Q1 = npn-Powertransistor [package="TO220 [THT]"]
  Q2 = npn-Powertransistor [package="TO220 [THT]"]
  Q3 = npn-Powertransistor [package="TO220 [THT]"]
  Q4 = npn-Powertransistor [package="TO220 [THT]"]
  Part1 = Arduino Uno (Rev3) - ICSP
  R1 = Resistor [tolerance=±5% resistance=1k package="1206 [SMD]"]

nets:
  N1: Q1.base, Part1.D6_PWM
  N2: Q1.emitter, Q2.emitter, Q3.emitter, Q4.emitter, Part1.GND
  N3: Q2.base, Part1.D9_PWM
  N4: Q3.base, Part1.D10_PWM/SS
  N5: Q4.base, Part1.D11_PWM/MOSI
  N6: Part1.D12/MISO, R1.Pin_1
  N7: Part1.D13/SCK, R1.Pin_0

notes:
  Capacitive Touch Object
  (Something Metal)
  RGBW LED Strip 12v
  Arduino needs to be Earth Grounded for Capacitive touch to read properly... So ground this to something physical, like yourself or a water pipe. You can also plug the arduino into a PC via USB and that will ground it properly, and in that case this isn't needed...
  12v Power Supply. I soldered a (pink) cable to the back of the Power Plug Socket, so it can power both the Arudino and the LED strip.
  ---->
